// Logisim project 16-bit Computer.circ as structural Verilog: 2 circuits, main circuit main
module main (
  input  Power,
  input  Manual_Override,
  output out_3,
  output out_4,
  output out_5,
  output out_6,
  output out_7,
  output out_8,
  output out_9,
  output out_10,
  output out_11,
  output out_12,
  output out_13,
  output out_14,
  output out_15,
  output out_16,
  output out_17,
  output out_18
);

  wire Clock_out, Manual_Tick_out, undriven, undriven_2, undriven_3, undriven_4;
  wire [15:0] AX_q, BX_q, CX_q, DX_q, or_2_out;

  Button Manual_Tick (.out(Manual_Tick_out));
  Clock Clock (.Power(Power), .Manual_Override(Manual_Override), .Manual_Tick(Manual_Tick_out), .Out(Clock_out));
  assign {out_3, out_4, out_5, out_6, out_7, out_8, out_9, out_10, out_11, out_12, out_13, out_14, out_15, out_16, out_17, out_18} = or_2_out;  // OR_Gate or_1, 16 bits wide OR_Gate
  assign or_2_out = DX_q | CX_q | BX_q | AX_q;  // OR_Gate or_2, 16 bits wide
  Register #(.width(16), .trigger("falling")) AX (
    .D({out_3, out_4, out_5, out_6, out_7, out_8, out_9, out_10, out_11, out_12, out_13, out_14, out_15, out_16, out_17, out_18}),
    .en(undriven), .Q(AX_q), .clk(Clock_out));  // open: clr
  Register #(.width(16), .trigger("falling")) BX (
    .D({out_3, out_4, out_5, out_6, out_7, out_8, out_9, out_10, out_11, out_12, out_13, out_14, out_15, out_16, out_17, out_18}),
    .en(undriven_2), .Q(BX_q), .clk(Clock_out));  // open: clr
  Register #(.width(16), .trigger("falling")) CX (
    .D({out_3, out_4, out_5, out_6, out_7, out_8, out_9, out_10, out_11, out_12, out_13, out_14, out_15, out_16, out_17, out_18}),
    .en(undriven_3), .Q(CX_q), .clk(Clock_out));  // open: clr
  Register #(.width(16), .trigger("falling")) DX (
    .D({out_3, out_4, out_5, out_6, out_7, out_8, out_9, out_10, out_11, out_12, out_13, out_14, out_15, out_16, out_17, out_18}),
    .en(undriven_4), .Q(DX_q), .clk(Clock_out));  // open: clr
endmodule

module Clock (
  input  Power,
  input  Manual_Override,
  input  Manual_Tick,
  output Out
);

  wire and_1_out, and_2_out, clock_1_out, not_1_out, or_1_out;

  Clock_part clock_1 (.out(clock_1_out));
  not not_1 (not_1_out, Manual_Override);
  and and_1 (and_1_out, not_1_out, clock_1_out);
  and and_2 (and_2_out, Manual_Override, Manual_Tick);
  or or_1 (or_1_out, and_1_out, and_2_out);
  and and_3 (Out, Power, or_1_out);
endmodule
